# Fritzing sketch powerstage (saved by Fritzing 0.9.10b)
breadboards: 1
perfboards: 1

parts:
  Q4 = PNP-Transistor [package="TO92 [THT]"]
  Q1 = MOSFET-NCHANNEL [package=to220v]
  R1 = Resistor [tolerance=±5% power=0.25 resistance=10k package=THT]
  R2 = Resistor [tolerance=±5% power=0.25 resistance=10k package=THT]
  Q5 = NPN-Transistor [package="TO92 [THT]"]
  Q6 = NPN-Transistor [package="TO92 [THT]"]
  Q7 = NPN-Transistor [package="TO92 [THT]"]
  R3 = Resistor [tolerance=±5% power=0.25 resistance=47k package=THT]
  J1 = female pin header, 3 pins [form="♀ (female)"]

nets:
  N1: Q4.E, Q1.G, Q5.E
  N2: Q4.B, R2.Pin_1, Q5.B, Q7.C
  N3: Q4.C, Q1.S, Q6.E, Q7.E, J1.pin1
  N4: R1.Pin_0, R2.Pin_0, Q5.C, J1.pin3
  N5: R1.Pin_1, Q6.C, Q7.B
  N6: Q6.B, R3.Pin_1
  N7: R3.Pin_0, J1.pin2
